# Fritzing sketch layout (saved by Fritzing 0.7.11b)
breadboards: 1

parts:
  RHT1 = Humidity and Temperature Sensor RHT03
  RHT2 = Humidity and Temperature Sensor RHT03
  Arduino_Ethernet_Shield1 = Arduino Ethernet Shield
  S1 = Pushbutton [package="[THT]"]
  SW1 = PowerSwitch Tail II

nets:
  VCC: RHT1.Vcc, RHT2.Vcc, Arduino_Ethernet_Shield1.SS, Arduino_Ethernet_Shield1.+5V, S1.Pin_1, S1.Pin_2
  N1: RHT1.Data-signal, Arduino_Ethernet_Shield1.D3
  N2: RHT1.GND_1, RHT1.GND_2, RHT2.GND_1, RHT2.GND_2, Arduino_Ethernet_Shield1.GND, S1.Pin_3, S1.Pin_4, SW1.-in, SW1.Ground
  N3: RHT2.Data-signal, Arduino_Ethernet_Shield1.D2
  N4: Arduino_Ethernet_Shield1.D1TX, SW1.+in
